# Fritzing sketch IR_bin (saved by Fritzing 0.8.7b)
breadboards: 1

parts:
  Componente1 = Arduino Uno (Rev3)
  J1 = Basic Servo
  Componente2 = SRF05 Ultrasonic Rangefinder
  R1 = Resistor [tolerance=±5% resistance=220 package=THT]
  J3 = Piezo Speaker
  Mod1 = KY-022 Infrared Receiver Module [package="Breakout board"]

nets:
  N1: Componente1.D9_PWM, J1.pulse
  N2: Componente1.D11_PWM/MOSI, Mod1.S
  N3: Componente1.D12/MISO, R1.Pin_0
  GND: Componente1.GND, J1.gnd, Componente2.GND, J3.pin1, Mod1.-
  N4: Componente1.D5_PWM, Componente2.Trig
  N5: Componente1.D6_PWM, Componente2.Echo
  3V3: Componente1.3V3, Mod1.Vin
  VCC: Componente1.5V, J1.vcc, Componente2.VCC
  N6: R1.Pin_1, J3.pin2

custom parts:
  KY-022 Infrared Receiver Module: KY-022 IR receiver module, reacts to 38kHz infrared light.
